# Fritzing sketch Party Button- Fritzing (saved by Fritzing 0.8.3b)
breadboards: 2

parts:
  Arduino_Uno = Arduino
  J1 = Piezo Speaker
  LED4 = RGB LED (com. cathode, rgb) [package="5 mm [THT]"]
  S1 = Pushbutton [package="[SMD]"]
  R1 = Resistor [tolerance=±5% resistance=220 package=THT]

nets:
  N1: Arduino_Uno.D5, LED4.green_anode
  N2: Arduino_Uno.D4, LED4.blue_anode
  N3: Arduino_Uno.D3, LED4.red_anode
  N4: Arduino_Uno.D2, Arduino_Uno.+5V, J1.pin2, S1.Pin_3, S1.Pin_4
  N5: Arduino_Uno.GND, J1.pin1, S1.Pin_1, S1.Pin_2, R1.Pin_1
  N6: LED4.common_cathode, R1.Pin_0

notes:
  Speaker will be underneath small breadboard
  Breadboard and speaker will be inside of the Easy Button
